# Fritzing sketch Lab5 (saved by Fritzing 0.9.3b)
breadboards: 2

parts:
  U1 = LM 358 Dual Op-Amp [part_number=LM358 package="DIP8 [THT]"]
  LMC1 = LMC7660 Switched Capacitor Voltage Converter [chip_label=LMC7660 package="DIP (Dual Inline) [THT]"]
  C1 = Electrolytic Capacitor [capacitance=10µF voltage=10V package="100 mil [THT, electrolytic]"]
  C2 = Electrolytic Capacitor [capacitance=10µF voltage=10V package="100 mil [THT, electrolytic]"]
  R1 = Resistor [tolerance=±5% resistance=1k package=THT]
  D1 = Rectifier Diode [part_number=1N4148 package="300 mil [THT]"]
  D2 = Rectifier Diode [part_number=1N4148 package="300 mil [THT]"]
  R2 = Resistor [tolerance=±5% resistance=1k package=THT]
  D3 = Rectifier Diode [part_number=1N4148 package="300 mil [THT]"]
  D4 = Rectifier Diode [part_number=1N4148 package="300 mil [THT]"]
  U2 = LM339N Quad Differential Comparators [chip_label=LM399N package="DIP (Dual Inline) [THT]"]
  R3 = Resistor [tolerance=±5% resistance=220 package=THT]
  R4 = Resistor [tolerance=±5% resistance=220 package=THT]
  D5 = Rectifier Diode [part_number=1N4148 package="300 mil [THT]"]
  R5 = Resistor [tolerance=±5% resistance=220 package=THT]
  C3 = Ceramic Capacitor [capacitance=100nF package="100 mil [THT, multilayer]"]
  D6 = Rectifier Diode [part_number=1N4148 package="300 mil [THT]"]
  R6 = Resistor [tolerance=±5% resistance=220 package=THT]
  C4 = Ceramic Capacitor [capacitance=100nF package="100 mil [THT, multilayer]"]
  D7 = Rectifier Diode [part_number=1N4148 package="300 mil [THT]"]
  D8 = Rectifier Diode [part_number=1N4148 package="300 mil [THT]"]
  R7 = Resistor [tolerance=±5% resistance=220 package=THT]
  R8 = Resistor [tolerance=±5% resistance=220 package=THT]
  C5 = Ceramic Capacitor [capacitance=100nF package="100 mil [THT, multilayer]"]
  C6 = Ceramic Capacitor [capacitance=100nF package="100 mil [THT, multilayer]"]
  U3 = LM 358 Dual Op-Amp [part_number=LM358 package="DIP8 [THT]"]

nets:
  Peak Detector 1: U1.connector0, U1.connector1, R1.Pin_1, D5.anode, U3.connector2
  Reference: U1.connector2
  N1: U1.connector3, LMC1.VOUT, C2.-
  Test: U1.connector4
  Peak Detector 2: U1.connector5, U1.connector6, R2.Pin_0, D6.anode, U3.connector4
  5V: U1.connector7, LMC1.V+, D1.cathode, D3.cathode, U2.VCC, R3.Pin_0, R4.Pin_0, U3.connector7
  N2: LMC1.CAP+, C1.+
  GND: LMC1.GND, C2.+, D2.anode, D4.anode, U2.1IN-, U2.3IN-, U2.GND, R5.Pin_1, C3.0, R6.Pin_1, C4.0
  N3: LMC1.CAP-, C1.-
  F38x ADC: R1.Pin_0, D1.anode, D2.cathode, R2.Pin_1, D3.anode, D4.cathode, U2.1IN+, U2.3IN+
  F38x: U2.1OUT, U2.OUT3, R3.Pin_1, R4.Pin_1
  ADC CH0: D5.cathode, R5.Pin_0, C3.1, R7.Pin_0, C5.1
  ADC CH1: D6.cathode, R6.Pin_0, C4.1, D8.cathode, R8.Pin_0, C6.1
  N4: D7.anode, U3.connector0, U3.connector1
  N5: D8.anode, U3.connector5, U3.connector6
  N6: R7.Pin_1, C5.0
  N7: R8.Pin_1, C6.0

notes:
  -5V
  V_r = (V_P-V_D)/(f*R*C)
  V_r = V_P/(f*R*C)
  Simple Peak Detector
  Precision Peak Detector
